# Fritzing sketch VpwShield (saved by Fritzing 0.9.4)
circuit board: 6.82674cm x 5.31381cm
breadboards: 1

parts:
  R6 = Resistor [tolerance=±5% resistance=47k package=THT]
  T2 = NPN-Transistor [part_number=BC548A package="TO92 [THT]"]
  R5 = Resistor [tolerance=±5% resistance=47k package=THT]
  R7 = Resistor [tolerance=±5% resistance=10k package=THT]
  T3 = NPN-Transistor [part_number=BC548A package="TO92 [THT]"]
  T4 = NPN-Transistor [part_number=BC548A package="TO92 [THT]"]
  J1 = screw terminal, 3 pins
  R8 = Resistor [tolerance=±5% resistance=47 package=THT]
  D3 = Rectifier Diode [part_number=1N4148 package="300 mil [THT]"]
  D4 = Zener Diode [part_number=ZPD8V2 breakdown_voltage=3.6V package="300 mil [THT]"]
  R9 = Resistor [tolerance=±5% resistance=510 package=THT]
  R10 = Resistor [tolerance=±5% resistance=1k package=THT]
  Part1 = Arduino Prototyping Shield

nets:
  N1: R6.Pin_0, T2.C, Part1.D7
  5V: R6.Pin_1, Part1.+5V
  GND: T2.E, R7.Pin_1, T4.E, J1.pin2, D4.anode, Part1.GND
  N2: T2.B, R5.Pin_1, R7.Pin_0
  N3: R5.Pin_0, J1.pin1, D3.cathode
  N4: T3.E, D3.anode, D4.cathode
  N5: T3.B, T4.C, R9.Pin_1
  N6: T3.C, R8.Pin_1
  N7: T4.B, R10.Pin_0
  12V: J1.pin3, R8.Pin_0, R9.Pin_0
  N8: R10.Pin_1, Part1.D6

notes:
  12V
  GND
  VPW
